# Fritzing sketch improved project 2 (saved by Fritzing 0.9.3b)
breadboards: 1

parts:
  Composant1 = Arduino Uno (Rev3)
  S1 = Pushbutton [package="[THT]"]
  S2 = Pushbutton [package="[THT]"]
  R1 = Resistor [tolerance=±5% resistance=220 package=THT]
  LED1 = LED - 5mm [color="Red (633nm)" package="5 mm [THT]"]
  LED2 = LED - 5mm [color="Red (633nm)" package="5 mm [THT]"]
  LED3 = LED - 5mm [color="Green (555nm)" package="5 mm [THT]"]
  R2 = Resistor [tolerance=±5% resistance=220 package=THT]
  R3 = Resistor [tolerance=±5% resistance=220 package=THT]
  R4 = Resistor [tolerance=±5% resistance=10k package=THT]
  R5 = Resistor [tolerance=±5% resistance=10k package=THT]

nets:
  N1: Composant1.D2, S1.Pin_1, S1.Pin_2, R5.Pin_0
  N2: Composant1.D3_PWM, LED3.anode
  N3: Composant1.D5_PWM, LED2.anode
  N4: Composant1.D6_PWM, LED1.anode
  N5: Composant1.D7, S2.Pin_3, S2.Pin_4, R4.Pin_0
  N6: Composant1.5V, S1.Pin_3, S1.Pin_4, S2.Pin_1, S2.Pin_2
  N7: Composant1.GND, R1.Pin_1, R2.Pin_1, R3.Pin_1, R4.Pin_1, R5.Pin_1
  N8: R1.Pin_0, LED3.cathode
  N9: LED1.cathode, R3.Pin_0
  N10: LED2.cathode, R2.Pin_0

// code stored in the sketch: arduino_project_2.ino
#define greenPin 3
#define redPin1 5
#define redPin2 6
#define brightnessLimit 250
#define redDelay 100

int switchState = LOW;
int before = 0;
int delta = 0;
int fadeDelay = redDelay;

int greenLevel = 0;

int activeLevel = 0;
int activeLed = redPin1;
int inactiveLevel = 0;
int inactiveLed = redPin2;
int switchLed = 0;
bool noDelay;

void setup() {
  pinMode(greenPin, OUTPUT);
  pinMode(redPin1, OUTPUT);
  pinMode(redPin2, OUTPUT);
  pinMode(2, INPUT);

  noDelay = true;
}

void loop() {
  switchState = digitalRead(2);

  noDelay = (digitalRead(7) == HIGH);

  delta = millis() - before;

 if(noDelay || delta > 1) {
    before = millis();
    
    if(switchState == LOW) {
      analogWrite(greenPin, greenLevel++);
      greenLevel = ensureBelowLimit(greenLevel);

      analogWrite(activeLed, activeLevel--);
      activeLevel = ensureOverZero(activeLevel);
      analogWrite(inactiveLed, inactiveLevel--);
      inactiveLevel = ensureOverZero(inactiveLevel);
    }
    else {
      if(activeLevel == brightnessLimit) {
        if(noDelay) {
          delay(250);
        }
        
        inactiveLevel = brightnessLimit;
        activeLevel = 0;
  
        switchLed = activeLed;
        activeLed = inactiveLed;
        inactiveLed = switchLed;

        fadeDelay = redDelay;
      }
      else if(fadeDelay-- < 0) {
        greenLevel = ensureOverZero(greenLevel-1);
        analogWrite(greenPin, greenLevel);
        
        analogWrite(activeLed, activeLevel++);
        activeLevel = ensureBelowLimit(activeLevel);
        analogWrite(inactiveLed, inactiveLevel--);
        inactiveLevel = ensureOverZero(inactiveLevel);
      }
    }
  }
}

int ensureOverZero(int level) {
  if(level < 0) {
    return 0;
  }
  else {
    return level;
  }
}

int ensureBelowLimit(int level) {
  if(level > brightnessLimit) {
    return brightnessLimit;
  }
  else {
    return level;
  }
}
